# Fritzing sketch retro-joystic-usb-adapter (saved by Fritzing 0.9.3b)

parts:
  Pro_Micro1 = Pro Micro
  X1 = DB9 Connector [package=db9]
  Select = SWITCH-MOMENTARY-2 [package=tactile_switch_smd-2]
  Start = SWITCH-MOMENTARY-2 [package=tactile_switch_smd-2]

nets:
  N1: Pro_Micro1.GND#3, Select.2, Start.2
  N2: Pro_Micro1.GND#4, X1.3
  N3: Pro_Micro1.D2, X1.9
  N4: Pro_Micro1.D3, X1.8
  N5: Pro_Micro1.D4, X1.7
  N6: Pro_Micro1.D5, X1.6
  N7: Pro_Micro1.D6, X1.1
  N8: Pro_Micro1.D7, Select.1
  N9: Pro_Micro1.D8, Start.1

notes:
  D-Sub 9-pin
  Pin Meaning Arduino Pin
  1 Up 2
  2 Down 3
  3 Left 4
  4 Right 5
  6 Fire 6
  8 GND
  Button Button Color Arduino Pin
  Select Red 7
  Start White 8

custom parts:
  Pro Micro: The SparkFun Pro Micro is a complete USB-based microcontoller development system, in a very small footprint, capable of implementing many types of projects. All programming can be done via the USB port.
